// Logisim project capstone-circuit.circ as structural Verilog: 5 circuits, main circuit main
module main (
  input  INVA,
  input  ENA,
  input  ENB,
  input  Carry_IN,
  input  [7:0] A,
  input  [7:0] B,
  input  F0,
  input  F1,
  output out_9,
  output out_10,
  output out_11,
  output out_12,
  output out_13,
  output out_14,
  output out_15,
  output out_16,
  output Carry_Out
);

  wire n1bit_alu_1_carry_out, n1bit_alu_2_carry_out, n1bit_alu_3_carry_out, n1bit_alu_4_carry_out,
       n1bit_alu_5_carry_out, n1bit_alu_6_carry_out, n1bit_alu_7_carry_out;

  _1bit_ALU u_1bit_alu_1 (
    .INVA(INVA), .A(A[0]), .ENA(ENA), .B(B[0]), .ENB(ENB), .F0(F0), .F1(F1), .Output(out_16),
    .Carry_Out(n1bit_alu_1_carry_out), .Carry_In(Carry_IN));
  _1bit_ALU u_1bit_alu_2 (
    .INVA(INVA), .A(A[1]), .ENA(ENA), .B(B[1]), .ENB(ENB), .F0(F0), .F1(F1), .Output(out_15),
    .Carry_Out(n1bit_alu_2_carry_out), .Carry_In(n1bit_alu_1_carry_out));
  _1bit_ALU u_1bit_alu_3 (
    .INVA(INVA), .A(A[2]), .ENA(ENA), .B(B[2]), .ENB(ENB), .F0(F0), .F1(F1), .Output(out_14),
    .Carry_Out(n1bit_alu_3_carry_out), .Carry_In(n1bit_alu_2_carry_out));
  _1bit_ALU u_1bit_alu_4 (
    .INVA(INVA), .A(A[3]), .ENA(ENA), .B(B[3]), .ENB(ENB), .F0(F0), .F1(F1), .Output(out_13),
    .Carry_Out(n1bit_alu_4_carry_out), .Carry_In(n1bit_alu_3_carry_out));
  _1bit_ALU u_1bit_alu_5 (
    .INVA(INVA), .A(A[4]), .ENA(ENA), .B(B[4]), .ENB(ENB), .F0(F0), .F1(F1), .Output(out_12),
    .Carry_Out(n1bit_alu_5_carry_out), .Carry_In(n1bit_alu_4_carry_out));
  _1bit_ALU u_1bit_alu_6 (
    .INVA(INVA), .A(A[5]), .ENA(ENA), .B(B[5]), .ENB(ENB), .F0(F0), .F1(F1), .Output(out_11),
    .Carry_Out(n1bit_alu_6_carry_out), .Carry_In(n1bit_alu_5_carry_out));
  _1bit_ALU u_1bit_alu_7 (
    .INVA(INVA), .A(A[6]), .ENA(ENA), .B(B[6]), .ENB(ENB), .F0(F0), .F1(F1), .Output(out_10),
    .Carry_Out(n1bit_alu_7_carry_out), .Carry_In(n1bit_alu_6_carry_out));
  _1bit_ALU u_1bit_alu_8 (
    .INVA(INVA), .A(A[7]), .ENA(ENA), .B(B[7]), .ENB(ENB), .F0(F0), .F1(F1), .Output(out_9),
    .Carry_Out(Carry_Out), .Carry_In(n1bit_alu_7_carry_out));
endmodule

module Logical_Unit (
  input  in_1,
  input  in_2,
  input  in_3,
  input  in_4,
  input  in_5,
  output out_6,
  output out_7,
  output out_8,
  output out_9,
  output out_10
);

  wire A___B_out, AB_out, Not_B_out;

  and AB (AB_out, in_1, in_2);
  or A___B (A___B_out, in_1, in_2);
  not Not_B (Not_B_out, in_2);
  and and_1 (out_6, AB_out, in_3);
  and and_2 (out_7, A___B_out, in_4);
  and and_3 (out_8, Not_B_out, in_5);

  assign out_9 = in_1;
  assign out_10 = in_2;
endmodule

module Full_Adder (
  input  in_1,
  input  in_2,
  input  in_3,
  input  in_4,
  output out_5,
  output out_6
);

  wire and_1_out, and_2_out, xor_1_out, xor_2_out;

  and and_1 (and_1_out, in_4, in_3, in_2);
  or or_1 (out_6, and_1_out, and_2_out);
  xor xor_1 (xor_1_out, in_2, in_3);
  and and_2 (and_2_out, in_4, xor_1_out, in_1);
  xor xor_2 (xor_2_out, in_1, xor_1_out);
  and and_3 (out_5, xor_2_out, in_4);
endmodule

module Decoder (
  input  in_1,
  input  in_2,
  output out_3,
  output out_4,
  output out_5,
  output out_6
);

  wire not_1_out, not_2_out;

  not not_1 (not_1_out, in_1);
  not not_2 (not_2_out, in_2);
  and and_1 (out_3, not_1_out, not_2_out);
  and and_2 (out_4, not_1_out, in_2);
  and and_3 (out_5, in_1, not_2_out);
  and and_4 (out_6, in_1, in_2);
endmodule

module _1bit_ALU (
  input  INVA,
  input  A,
  input  Carry_In,
  input  ENA,
  input  B,
  input  ENB,
  input  F0,
  input  F1,
  output Output,
  output Carry_Out
);

  wire and_1_out, and_2_out, DC_out_3, DC_out_4, DC_out_5, DC_out_6, FA_out_5, LU_out_6, LU_out_7, LU_out_8,
       LU_out_9, LU_out_10, xor_1_out;

  and and_1 (and_1_out, A, ENA);
  xor xor_1 (xor_1_out, INVA, and_1_out);
  and and_2 (and_2_out, B, ENB);
  Logical_Unit LU (
    .in_1(xor_1_out), .in_2(and_2_out), .out_6(LU_out_6), .out_7(LU_out_7), .out_8(LU_out_8),
    .out_9(LU_out_9), .out_10(LU_out_10), .in_3(DC_out_3), .in_4(DC_out_4), .in_5(DC_out_5));
  Decoder DC (.out_3(DC_out_3), .out_4(DC_out_4), .out_5(DC_out_5), .out_6(DC_out_6), .in_1(F0), .in_2(F1));
  Full_Adder FA (
    .in_2(LU_out_10), .in_3(LU_out_9), .in_4(DC_out_6), .in_1(Carry_In), .out_5(FA_out_5), .out_6(Carry_Out));
  or or_1 (Output, LU_out_6, LU_out_7, LU_out_8, FA_out_5);
endmodule
